# Fritzing sketch ArduinoScheme (saved by Fritzing 0.9.3b)
breadboards: 1

parts:
  Componente1 = Arduino Uno (Rev3)
  Componente2 = Bluetooth HC-05 Macho  # not connected
  LED1 = RGB LED (com. cathode, rgb) [package="5 mm [THT]"]
  R1 = Resistor [tolerance=±5% resistance=220 package=THT]
  R2 = Resistor [tolerance=±5% resistance=220 package=THT]
  R3 = Resistor [tolerance=±5% resistance=220 package=THT]

nets:
  N1: Componente1.D9_PWM, Componente1.GND
  N2: LED1.red_anode, LED1.common_cathode, LED1.green_anode, LED1.blue_anode
  N3: R1.Pin_0, R2.Pin_1, R3.Pin_1
  N4: R1.Pin_1, R2.Pin_0, R3.Pin_0
